# Fritzing sketch schematic (saved by Fritzing 0.9.3b)

parts:
  Part1 = Barometric Pressure Sensor - BMP180 Breakout (GY-68)
  M1 = DOIT Esp32 DevKit v1 (30 pins long, 11 pins width) [part_number=ESP32S-PIN30]

nets:
  VCC: Part1.VCC, M1.3V3
  GND: Part1.GND, M1.GND
  N1: Part1.SCL, M1.D22
  N2: Part1.SDA, M1.D21

custom parts:
  DOIT Esp32 DevKit v1 (30 pins long, 11 pins width): The DOIT Esp32 DevKit v1 is one of the development board created by DOIT to evaluate the ESP-WROOM-32 module. It is based on the ESP32 microcontroller that boasts Wifi, Bluetooth, Ethernet and Low Power support all in a single chip. (vanepp) made breadboard work, adjusted pin numbering and labels and reduced size of schematic and cleaned up pcb. This chip is 30pins long (2 x15) and 11 pins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
